// Logisim project cpu.circ as structural Verilog: 4 circuits, main circuit main
module main (
  input  [31:0] INSTRUCTION,
  input  CLOCK,
  output [31:0] FETCH_ADDRESS,
  output [31:0] ra,
  output [31:0] sp,
  output [31:0] t0,
  output [31:0] t1,
  output [31:0] t2,
  output [31:0] s0,
  output [31:0] s1,
  output [31:0] a0
);

  wire branch_comparison_1_breq, branch_comparison_1_brlt, control_module_1_asel, control_module_1_brun,
       control_module_1_bsel, control_module_1_memrw, control_module_1_regwen, lb, lh, pc_sel;
  wire [1:0] control_module_1_wbsel, offset;
  wire [2:0] control_module_1_immsel;
  wire [3:0] control_module_1_alusel;
  wire [7:0] multiplexer_5_out;
  wire [15:0] multiplexer_6_out;
  wire [31:0] ALU_4, ALU_RESULT, bit_extender_2_out, bit_extender_3_out, divider_1_rem, IMM, instruction_p,
       main_1_read_data_1, main_1_read_data_2, MEM, MEM_RESULT, multiplexer_1_out, multiplexer_2_out,
       multiplexer_3_out, multiplexer_4_out, multiplexer_8_out, pc4, pc4_p, pc_p, PC_q;

  Multiplexer #(.width(32), .enable("false")) multiplexer_1 (
    .in0(INSTRUCTION), .in1({32{1'b0}}), .out(multiplexer_1_out), .sel(pc_sel));
  Register #(.width(32)) register_1 (.D(multiplexer_1_out), .clk(CLOCK), .Q(instruction_p));  // open: en, clr
  Divider #(.width(32)) divider_1 (.a(IMM), .b(32'h4), .rem(divider_1_rem));  // open: out, upper
  Bit_Extender #(.in_width(32), .out_width(2)) bit_extender_1 (.in(divider_1_rem), .out(offset));
  IMM_GEN imm_gen_1 (.INSTRUCTION(instruction_p[31:7]), .ImmSel(control_module_1_immsel), .IMM(IMM));
  Multiplexer #(.width(32), .enable("false")) multiplexer_2 (
    .in0(main_1_read_data_1), .in1(pc_p), .out(multiplexer_2_out), .sel(control_module_1_asel));
  Multiplexer #(.width(32), .enable("false")) multiplexer_3 (
    .in0(main_1_read_data_2), .in1(IMM), .out(multiplexer_3_out), .sel(control_module_1_bsel));
  regfile_main main_1 (
    .Read_Register_1_rs1(instruction_p[19:15]), .Read_Register_2_rs2(instruction_p[24:20]),
    .Write_Register_rd(instruction_p[11:7]), .Write_Data(multiplexer_8_out),
    .Write_Enable(control_module_1_regwen), .Clock(CLOCK), .Read_Data_1(main_1_read_data_1),
    .Read_Data_2(main_1_read_data_2), .ra(ra), .sp(sp), .t0(t0), .t1(t1), .t2(t2), .s0(s0), .s1(s1), .a0(a0));
  control_module control_module_1 (
    .INSTRUCTION(instruction_p), .BrEq(branch_comparison_1_breq), .BrLT(branch_comparison_1_brlt),
    .PC_SEL(pc_sel), .ImmSel(control_module_1_immsel), .RegWEn(control_module_1_regwen),
    .BrUn(control_module_1_brun), .BSel(control_module_1_bsel), .ASel(control_module_1_asel),
    .ALUSel(control_module_1_alusel), .MemRW(control_module_1_memrw), .WBSel(control_module_1_wbsel),
    .lb(lb), .lh(lh));
  Branch_Comparison branch_comparison_1 (
    .A(main_1_read_data_1), .B(main_1_read_data_2), .BrUn(control_module_1_brun),
    .BrLT(branch_comparison_1_brlt), .BrEq(branch_comparison_1_breq));
  Adder #(.width(32)) adder_1 (.a(PC_q), .b(32'h4), .out(pc4));  // open: cin, cout
  Multiplexer #(.width(32), .enable("false")) multiplexer_4 (
    .in0(pc4), .in1(ALU_RESULT), .out(multiplexer_4_out), .sel(pc_sel));
  alu alu_1 (.A(multiplexer_2_out), .B(multiplexer_3_out), .ALUSel(control_module_1_alusel), .Result(ALU_RESULT));
  Register #(.width(32)) PC (.D(multiplexer_4_out), .en(1'b1), .clk(CLOCK), .Q(PC_q));  // open: clr
  assign bit_extender_2_out = {{24{multiplexer_5_out[7]}}, multiplexer_5_out};  // Bit_Extender bit_extender_2
  Multiplexer #(.select(2), .width(8), .enable("false")) multiplexer_5 (
    .in0(MEM[7:0]), .in1(MEM[15:8]), .in2(MEM[23:16]), .in3(MEM[31:24]), .out(multiplexer_5_out), .sel(offset));
  Multiplexer #(.select(2), .width(16), .enable("false")) multiplexer_6 (
    .in0(MEM[15:0]), .in2(MEM[31:16]), .out(multiplexer_6_out), .sel(offset));  // open: in1, in3
  assign bit_extender_3_out = {{16{multiplexer_6_out[15]}}, multiplexer_6_out};  // Bit_Extender bit_extender_3
  Multiplexer #(.select(2), .width(32), .enable("false")) multiplexer_7 (
    .in0(MEM), .in1(bit_extender_3_out), .in2(bit_extender_2_out), .out(MEM_RESULT), .sel({lb, lh}));  // open: in3
  Register #(.width(32)) register_2 (.D(PC_q), .en(1'b1), .clk(CLOCK), .Q(pc_p));  // open: clr
  Divider #(.width(32)) divider_2 (.a(PC_q), .b(32'h4), .out(FETCH_ADDRESS));  // open: upper, rem
  Divider #(.width(32)) divider_3 (.a(ALU_RESULT), .b(32'h4), .out(ALU_4));  // open: upper, rem
  // mem_main MEM: pin names not known; wires that end beside it: ALU_4, main_1_read_data_2, control_module_1_memrw, CLOCK, MEM
  Adder #(.width(32)) adder_2 (.a(pc_p), .b(32'h4), .out(pc4_p));  // open: cin, cout
  Multiplexer #(.select(2), .width(32), .enable("false")) multiplexer_8 (
    .in0(MEM_RESULT), .in1(ALU_RESULT), .in2(pc4_p), .out(multiplexer_8_out), .sel(control_module_1_wbsel));  // open: in3

  // Other names for the same wires on the sheet: clk = CLOCK; fetch_addr[31:0] = FETCH_ADDRESS;
  //   MEMSel[1:0] = {lb, lh}; x1[31:0] = ra; x2[31:0] = sp; x5[31:0] = t0; x6[31:0] = t1; x7[31:0] = t2;
  //   x8[31:0] = s0; x9[31:0] = s1; x10[31:0] = a0

  // Notes on the sheet:
  //   Output
  //   Inputs/Outputs from run.circ. DO NOT MOVE THESE.
  //   Inputs
  //   ASel
  //   BSel
  //   Inputs/Outputs from run.circ. DO NOT MOVE THESE.
endmodule

module control_module (
  input  [31:0] INSTRUCTION,
  input  BrEq,
  input  BrLT,
  output PC_SEL,
  output [2:0] ImmSel,
  output RegWEn,
  output BrUn,
  output BSel,
  output ASel,
  output [3:0] ALUSel,
  output MemRW,
  output [1:0] WBSel,
  output lb,
  output lh
);

  wire add, addi, and_43a5541d, andi, ASEL_beq, ASEL_blt, ASEL_bne, ASEL_JAL, ASEL_lui, BSEL_R,
       comparator_1_eq, comparator_2_eq, comparator_3_eq, comparator_4_eq, comparator_5_eq, comparator_6_eq,
       comparator_7_eq, comparator_8_eq, comparator_9_eq, comparator_10_eq, comparator_11_eq,
       comparator_12_eq, comparator_13_eq, comparator_22_eq, comparator_23_eq, comparator_24_eq,
       comparator_25_eq, comparator_26_eq, comparator_27_eq, comparator_28_eq, comparator_29_eq,
       comparator_30_eq, comparator_31_eq, comparator_32_eq, comparator_33_eq, comparator_34_eq,
       comparator_35_eq, comparator_36_eq, comparator_37_eq, comparator_38_eq, comparator_39_eq,
       comparator_40_eq, comparator_41_eq, comparator_42_eq, comparator_43_eq, comparator_44_eq,
       comparator_45_eq, comparator_46_eq, comparator_47_eq, comparator_48_eq, comparator_49_eq,
       comparator_50_eq, div, First_Bit, First_bit_t, I, I_JALR, Load, lw, mul, mulh, nor_1_out, nor_3_out,
       not_1_out, or_1_out, or_7a9453ae, or_10_out, or_11_out, or_12_out, or_13_out, or_14_out, or_15_out,
       or_16_out, or_17_out, ori, PCSEL_beq, PCSEL_blt, PCSEL_bltu, PCSEL_bne, rem_182249c3, SB,
       sll_cdbb09a6, slli, slt, slti, srai, srl_7628d6ca, srli, sub, xor_624519b2, xori;

  Comparator #(.width(7)) comparator_1 (.a(INSTRUCTION[31:25]), .b(7'b0100000), .eq(comparator_1_eq));  // open: gt, lt
  Comparator #(.width(7)) comparator_2 (.a(INSTRUCTION[31:25]), .b({7{1'b0}}), .eq(comparator_2_eq));  // open: gt, lt
  Comparator #(.width(7)) comparator_3 (.a(INSTRUCTION[31:25]), .b(7'b0000001), .eq(comparator_3_eq));  // open: gt, lt
  Comparator #(.width(7)) comparator_4 (.a(INSTRUCTION[31:25]), .b({7{1'b0}}), .eq(comparator_4_eq));  // open: gt, lt
  Comparator #(.width(7)) comparator_5 (.a(INSTRUCTION[31:25]), .b({7{1'b0}}), .eq(comparator_5_eq));  // open: gt, lt
  Comparator #(.width(7)) comparator_6 (.a(INSTRUCTION[31:25]), .b(7'b0000001), .eq(comparator_6_eq));  // open: gt, lt
  Comparator #(.width(7)) comparator_7 (.a(INSTRUCTION[31:25]), .b({7{1'b0}}), .eq(comparator_7_eq));  // open: gt, lt
  Comparator #(.width(7)) comparator_8 (.a(INSTRUCTION[31:25]), .b({7{1'b0}}), .eq(comparator_8_eq));  // open: gt, lt
  Comparator #(.width(7)) comparator_9 (.a(INSTRUCTION[31:25]), .b(7'b0000001), .eq(comparator_9_eq));  // open: gt, lt
  Comparator #(.width(7)) comparator_10 (.a(INSTRUCTION[31:25]), .b({7{1'b0}}), .eq(comparator_10_eq));  // open: gt, lt
  Comparator #(.width(7)) comparator_11 (.a(INSTRUCTION[31:25]), .b({7{1'b0}}), .eq(comparator_11_eq));  // open: gt, lt
  Comparator #(.width(7)) comparator_12 (.a(INSTRUCTION[31:25]), .b({7{1'b0}}), .eq(comparator_12_eq));  // open: gt, lt
  Comparator #(.width(7)) comparator_13 (
    .a(INSTRUCTION[31:25]), .b(7'b0100000), .eq(comparator_13_eq));  // open: gt, lt
  Comparator #(.width(7)) comparator_14 (.a(INSTRUCTION[6:0]), .b(7'b0110011), .eq(BSEL_R));  // open: gt, lt
  Comparator #(.width(7)) comparator_15 (.a(INSTRUCTION[6:0]), .b(7'b0000011), .eq(Load));  // open: gt, lt
  Comparator #(.width(7)) comparator_16 (.a(INSTRUCTION[6:0]), .b(7'b0010011), .eq(I));  // open: gt, lt
  Comparator #(.width(7)) comparator_17 (.a(INSTRUCTION[6:0]), .b(7'b0100011), .eq(MemRW));  // open: gt, lt
  Comparator #(.width(7)) comparator_18 (.a(INSTRUCTION[6:0]), .b(7'b1100011), .eq(SB));  // open: gt, lt
  Comparator #(.width(7)) comparator_19 (.a(INSTRUCTION[6:0]), .b(7'b0110111), .eq(ASEL_lui));  // open: gt, lt
  Comparator #(.width(7)) comparator_20 (.a(INSTRUCTION[6:0]), .b(7'b1101111), .eq(ASEL_JAL));  // open: gt, lt
  Comparator #(.width(7)) comparator_21 (.a(INSTRUCTION[6:0]), .b(7'b1100111), .eq(I_JALR));  // open: gt, lt
  Comparator #(.width(3)) comparator_22 (.a(INSTRUCTION[14:12]), .b(3'b000), .eq(comparator_22_eq));  // open: gt, lt
  Comparator #(.width(7)) comparator_23 (.a(INSTRUCTION[31:25]), .b({7{1'b0}}), .eq(comparator_23_eq));  // open: gt, lt
  Comparator #(.width(3)) comparator_24 (.a(INSTRUCTION[14:12]), .b(3'b000), .eq(comparator_24_eq));  // open: gt, lt
  Comparator #(.width(7)) comparator_25 (
    .a(INSTRUCTION[31:25]), .b(7'b0000001), .eq(comparator_25_eq));  // open: gt, lt
  Comparator #(.width(3)) comparator_26 (.a(INSTRUCTION[14:12]), .b(3'b000), .eq(comparator_26_eq));  // open: gt, lt
  Comparator #(.width(3)) comparator_27 (.a(INSTRUCTION[14:12]), .b(3'b001), .eq(comparator_27_eq));  // open: gt, lt
  Comparator #(.width(3)) comparator_28 (.a(INSTRUCTION[14:12]), .b(3'b001), .eq(comparator_28_eq));  // open: gt, lt
  Comparator #(.width(3)) comparator_29 (.a(INSTRUCTION[14:12]), .b(3'b010), .eq(comparator_29_eq));  // open: gt, lt
  Comparator #(.width(3)) comparator_30 (.a(INSTRUCTION[14:12]), .b(3'b100), .eq(comparator_30_eq));  // open: gt, lt
  Comparator #(.width(3)) comparator_31 (.a(INSTRUCTION[14:12]), .b(3'b100), .eq(comparator_31_eq));  // open: gt, lt
  Comparator #(.width(3)) comparator_32 (.a(INSTRUCTION[14:12]), .b(3'b101), .eq(comparator_32_eq));  // open: gt, lt
  Comparator #(.width(3)) comparator_33 (.a(INSTRUCTION[14:12]), .b(3'b110), .eq(comparator_33_eq));  // open: gt, lt
  Comparator #(.width(3)) comparator_34 (.a(INSTRUCTION[14:12]), .b(3'b110), .eq(comparator_34_eq));  // open: gt, lt
  Comparator #(.width(3)) comparator_35 (.a(INSTRUCTION[14:12]), .b(3'b111), .eq(comparator_35_eq));  // open: gt, lt
  Comparator #(.width(3)) comparator_36 (.a(INSTRUCTION[14:12]), .b(3'b000), .eq(comparator_36_eq));  // open: gt, lt
  Comparator #(.width(3)) comparator_37 (.a(INSTRUCTION[14:12]), .b(3'b001), .eq(comparator_37_eq));  // open: gt, lt
  Comparator #(.width(3)) comparator_38 (.a(INSTRUCTION[14:12]), .b(3'b010), .eq(comparator_38_eq));  // open: gt, lt
  Comparator #(.width(3)) comparator_39 (.a(INSTRUCTION[14:12]), .b(3'b000), .eq(comparator_39_eq));  // open: gt, lt
  Comparator #(.width(3)) comparator_40 (.a(INSTRUCTION[14:12]), .b(3'b001), .eq(comparator_40_eq));  // open: gt, lt
  Comparator #(.width(3)) comparator_41 (.a(INSTRUCTION[14:12]), .b(3'b010), .eq(comparator_41_eq));  // open: gt, lt
  Comparator #(.width(3)) comparator_42 (.a(INSTRUCTION[14:12]), .b(3'b100), .eq(comparator_42_eq));  // open: gt, lt
  Comparator #(.width(3)) comparator_43 (.a(INSTRUCTION[14:12]), .b(3'b101), .eq(comparator_43_eq));  // open: gt, lt
  Comparator #(.width(3)) comparator_44 (.a(INSTRUCTION[14:12]), .b(3'b001), .eq(comparator_44_eq));  // open: gt, lt
  Comparator #(.width(3)) comparator_45 (.a(INSTRUCTION[14:12]), .b(3'b110), .eq(comparator_45_eq));  // open: gt, lt
  Comparator #(.width(3)) comparator_46 (.a(INSTRUCTION[14:12]), .b(3'b111), .eq(comparator_46_eq));  // open: gt, lt
  Comparator #(.width(3)) comparator_47 (.a(INSTRUCTION[14:12]), .b(3'b000), .eq(comparator_47_eq));  // open: gt, lt
  Comparator #(.width(3)) comparator_48 (.a(INSTRUCTION[14:12]), .b(3'b100), .eq(comparator_48_eq));  // open: gt, lt
  Comparator #(.width(3)) comparator_49 (.a(INSTRUCTION[14:12]), .b(3'b110), .eq(comparator_49_eq));  // open: gt, lt
  Comparator #(.width(3)) comparator_50 (.a(INSTRUCTION[14:12]), .b(3'b001), .eq(comparator_50_eq));  // open: gt, lt
  and and_1 (add, comparator_22_eq, comparator_23_eq);
  and and_2 (mul, comparator_24_eq, BSEL_R, comparator_25_eq);
  and and_3 (sub, comparator_26_eq, BSEL_R, comparator_1_eq);
  and and_4 (sll_cdbb09a6, comparator_27_eq, BSEL_R, comparator_2_eq);
  and and_5 (mulh, comparator_28_eq, BSEL_R, comparator_3_eq);
  and and_6 (slt, comparator_29_eq, BSEL_R, comparator_4_eq);
  and and_7 (xor_624519b2, comparator_30_eq, BSEL_R, comparator_5_eq);
  and and_8 (div, comparator_31_eq, BSEL_R, comparator_6_eq);
  and and_9 (srl_7628d6ca, comparator_32_eq, BSEL_R, comparator_7_eq);
  and and_10 (or_7a9453ae, comparator_33_eq, BSEL_R, comparator_8_eq);
  and and_11 (rem_182249c3, comparator_34_eq, BSEL_R, comparator_9_eq);
  and and_12 (and_43a5541d, comparator_35_eq, BSEL_R, comparator_10_eq);
  and and_13 (lb, comparator_36_eq, Load);
  and and_14 (lh, comparator_37_eq, Load);
  and and_15 (lw, comparator_38_eq, Load);
  and and_16 (addi, comparator_39_eq, I);
  and and_17 (slli, comparator_40_eq, I, comparator_11_eq);
  and and_18 (slti, comparator_41_eq, I);
  and and_19 (xori, comparator_42_eq, I);
  and and_20 (srli, comparator_43_eq, I, comparator_12_eq);
  and and_21 (srai, comparator_44_eq, I, comparator_13_eq);
  and and_22 (ori, comparator_45_eq, I);
  and and_23 (andi, comparator_46_eq, I);
  and and_24 (ASEL_beq, comparator_47_eq, SB);
  and and_25 (ASEL_blt, comparator_48_eq, SB);
  and and_26 (BrUn, comparator_49_eq, SB);
  and and_27 (ASEL_bne, comparator_50_eq, SB);
  not not_1 (not_1_out, BrEq);
  and and_28 (PCSEL_bltu, BrLT, BrUn);
  and and_29 (PCSEL_beq, BrEq, ASEL_beq);
  and and_30 (PCSEL_bne, not_1_out, ASEL_beq);
  and and_31 (PCSEL_blt, BrLT, ASEL_blt);
  or or_1 (or_1_out, BSEL_R, I);
  nor nor_1 (nor_1_out, lh, lb, lw, First_bit_t);
  or or_2 (WBSel[1], ASEL_JAL, I_JALR);
  or or_3 (First_bit_t, ASEL_JAL, I_JALR);
  or or_4 (ImmSel[0], Load, I, SB, I_JALR, ASEL_lui);
  or or_5 (ImmSel[1], MemRW, SB);
  or or_6 (ImmSel[2], ASEL_lui, ASEL_JAL);
  or or_7 (WBSel[0], nor_1_out, or_1_out);
  not not_2 (BSel, BSEL_R);
  nor nor_2 (RegWEn, MemRW, ASEL_beq, ASEL_bne, BrUn, ASEL_blt);
  or or_8 (ASel, BrUn, ASEL_beq, ASEL_blt, ASEL_bne, ASEL_JAL, ASEL_lui);
  or or_9 (PC_SEL, PCSEL_beq, PCSEL_blt, PCSEL_bltu, PCSEL_bne, ASEL_JAL, I_JALR);
  or or_10 (or_10_out, slt, slti);
  or or_11 (or_11_out, srli, srl_7628d6ca);
  or or_12 (or_12_out, and_43a5541d, andi);
  or or_13 (or_13_out, xor_624519b2, xori);
  or or_14 (or_14_out, or_7a9453ae, ori);
  or or_15 (or_15_out, xor_624519b2, xori);
  or or_16 (or_16_out, slli, sll_cdbb09a6, slti, slt);
  nor nor_3 (nor_3_out, add, addi, Load, MemRW, First_Bit, SB, ASEL_lui, ASEL_JAL, I_JALR);
  or or_17 (or_17_out, slli, sll_cdbb09a6, slti, slt, mul, mulh);
  or or_18 (ALUSel[0], srai, nor_3_out, or_12_out, or_13_out, or_10_out, rem_182249c3, mulh, ASEL_lui);
  or or_19 (ALUSel[1], or_14_out, or_15_out, or_17_out);
  or or_20 (ALUSel[2], or_16_out, or_11_out, srai, sub, ASEL_lui);
  or or_21 (ALUSel[3], mul, div, rem_182249c3, mulh, sub, ASEL_lui);
  or or_22 (First_Bit, sll_cdbb09a6, div, sub, or_7a9453ae, mul, srli, srl_7628d6ca, slli, ori);

  // Other names for the same wires on the sheet: beq = ASEL_beq; RegWEn_beq = ASEL_beq; blt = ASEL_blt;
  //   RegWEn_blt = ASEL_blt; ASEL_bltu = BrUn; bltu = BrUn; BrUn_bltu = BrUn; RegWEn_bltu = BrUn; bne = ASEL_bne;
  //   RegWEn_bne = ASEL_bne; opcode[6:0] = INSTRUCTION[6:0]; funct3[2:0] = INSTRUCTION[14:12];
  //   funct7[6:0] = INSTRUCTION[31:25]; PCSEL_JALR = I_JALR; R = BSEL_R; MemRW_store = MemRW; RegWEn_sw = MemRW;
  //   S_STORE = MemRW; U_LUI = ASEL_lui; PCSEL_JAL = ASEL_JAL; UJ_JAL = ASEL_JAL

  // Notes on the sheet:
  //   INPUTS to your circuit
  //   Type
  //   Check
  //   OUTPUT from your circuit
endmodule

module IMM_GEN (
  input  [24:0] INSTRUCTION,
  input  [2:0] ImmSel,
  output [31:0] IMM
);

  wire [31:0] I_IMM, S_IMM, SB_IMM, UJ_IMM;

  assign I_IMM = {{20{INSTRUCTION[24]}}, INSTRUCTION[24:13]};  // Bit_Extender bit_extender_1
  Multiplexer #(.select(3), .width(32), .enable("false")) multiplexer_1 (
    .in1(I_IMM), .in2(S_IMM), .in3(SB_IMM), .in4(UJ_IMM), .in5({INSTRUCTION[24:5], {12{1'b0}}}), .out(IMM),
    .sel(ImmSel));  // open: in0, in6, in7
  assign S_IMM = {{20{INSTRUCTION[24]}}, {INSTRUCTION[24:18], INSTRUCTION[4:0]}};  // Bit_Extender bit_extender_2
  assign SB_IMM = {{19{INSTRUCTION[24]}}, {INSTRUCTION[24], INSTRUCTION[0], INSTRUCTION[23:18], INSTRUCTION[4:1], 1'b0}};  // Bit_Extender bit_extender_3
  assign UJ_IMM = {{11{INSTRUCTION[24]}}, {INSTRUCTION[24], INSTRUCTION[12:5], INSTRUCTION[13], INSTRUCTION[23:14], 1'b0}};  // Bit_Extender bit_extender_4

  // Other names for the same wires on the sheet: U_IMM[31:12] = INSTRUCTION[24:5]

  // Notes on the sheet:
  //   INPUTS to your circuit
  //   OUTPUT from your circuit
endmodule

module Branch_Comparison (
  input  [31:0] A,
  input  [31:0] B,
  input  BrUn,
  output BrLT,
  output BrEq
);

  wire BrLT_Signed, BrLT_Unsigned;

  Comparator #(.width(32)) comparator_1 (.a(A), .b(B), .lt(BrLT_Signed));  // open: gt, eq
  Multiplexer #(.enable("false")) multiplexer_1 (.in0(BrLT_Signed), .in1(BrLT_Unsigned), .out(BrLT), .sel(BrUn));
  Comparator #(.width(32), .mode("unsigned")) comparator_2 (.a(A), .b(B), .lt(BrLT_Unsigned));  // open: gt, eq
  Comparator #(.width(32)) comparator_3 (.a(A), .b(B), .eq(BrEq));  // open: gt, lt

  // Notes on the sheet:
  //   INPUTS to your circuit
  //   OUTPUT from your circuit
endmodule
