// Logisim project regfile.circ as structural Verilog: 1 circuit, main circuit main
module main (
  input  [4:0] Read_Register_1_rs1,
  input  [4:0] Read_Register_2_rs2,
  input  [4:0] Write_Register_rd,
  input  [31:0] Write_Data,
  input  Write_Enable,
  input  Clock,
  output [31:0] ra,
  output [31:0] sp,
  output [31:0] t0,
  output [31:0] t1,
  output [31:0] t2,
  output [31:0] s0,
  output [31:0] s1,
  output [31:0] a0,
  output [31:0] Read_Data_1,
  output [31:0] Read_Data_2
);

  wire and_1_out, and_2_out, and_3_out, and_4_out, and_5_out, and_6_out, and_7_out, and_8_out, write_a0,
       write_ra, write_s0, write_s1, write_sp, write_t0, write_t1, write_t2;
  wire [31:0] zero;

  Demultiplexer #(.select(5), .enable("false")) demultiplexer_1 (
    .out1(write_ra), .out2(write_sp), .out5(write_t0), .out6(write_t1), .out7(write_t2), .out8(write_s0),
    .out9(write_s1), .out10(write_a0), .sel(Write_Register_rd));  // open: out0, out3, out4, out11, out12, out13, out14, out15, out16, out17, out18, out19, out20, out21, out22, out23, out24, out25, out26, out27, out28, out29, out30, out31, in
  Register #(.width(32)) x0 (.D({32{1'b0}}), .clk(Clock), .Q(zero));  // open: en, clr
  and and_1 (and_1_out, Write_Enable, write_ra);
  and and_2 (and_2_out, Write_Enable, write_t0);
  and and_3 (and_3_out, Write_Enable, write_t2);
  and and_4 (and_4_out, Write_Enable, write_s1);
  Register #(.width(32)) x1 (.D(Write_Data), .en(and_1_out), .clk(Clock), .Q(ra));  // open: clr
  Register #(.width(32)) x5 (.D(Write_Data), .en(and_2_out), .clk(Clock), .Q(t0));  // open: clr
  Register #(.width(32)) x7 (.D(Write_Data), .en(and_3_out), .clk(Clock), .Q(t2));  // open: clr
  Register #(.width(32)) x9 (.D(Write_Data), .en(and_4_out), .clk(Clock), .Q(s1));  // open: clr
  Multiplexer #(.select(5), .width(32), .enable("false")) multiplexer_1 (
    .in0(zero), .in1(ra), .in2(sp), .in5(t0), .in6(t1), .in7(t2), .in8(s0), .in9(s1), .in10(a0),
    .out(Read_Data_1), .sel(Read_Register_1_rs1));  // open: in3, in4, in11, in12, in13, in14, in15, in16, in17, in18, in19, in20, in21, in22, in23, in24, in25, in26, in27, in28, in29, in30, in31
  Register #(.width(32)) x2 (.D(Write_Data), .en(and_5_out), .clk(Clock), .Q(sp));  // open: clr
  and and_5 (and_5_out, Write_Enable, write_sp);
  Register #(.width(32)) x6 (.D(Write_Data), .en(and_6_out), .clk(Clock), .Q(t1));  // open: clr
  and and_6 (and_6_out, Write_Enable, write_t1);
  Register #(.width(32)) x8 (.D(Write_Data), .en(and_7_out), .clk(Clock), .Q(s0));  // open: clr
  and and_7 (and_7_out, Write_Enable, write_s0);
  Register #(.width(32)) x10 (.D(Write_Data), .en(and_8_out), .clk(Clock), .Q(a0));  // open: clr
  and and_8 (and_8_out, Write_Enable, write_a0);
  Multiplexer #(.select(5), .width(32), .enable("false")) multiplexer_2 (
    .in0(zero), .in1(ra), .in2(sp), .in5(t0), .in6(t1), .in7(t2), .in8(s0), .in9(s1), .in10(a0),
    .out(Read_Data_2), .sel(Read_Register_2_rs2));  // open: in3, in4, in11, in12, in13, in14, in15, in16, in17, in18, in19, in20, in21, in22, in23, in24, in25, in26, in27, in28, in29, in30, in31

  // Other names for the same wires on the sheet: clk = Clock; read_data1[31:0] = Read_Data_1;
  //   read_data2[31:0] = Read_Data_2; read_reg1[4:0] = Read_Register_1_rs1; read_reg2[4:0] = Read_Register_2_rs2;
  //   write_en = Write_Enable; write_reg[4:0] = Write_Register_rd

  // Notes on the sheet:
  //   INPUTS to your circuit
  //   DON'T CHANGE THE LOCATIONS OF THE INPUTS AND OUTPUTS!
  //   These are DEBUG/TEST outputs from your circuit.
  //   OUTPUTS from your circuit
endmodule
