// Logisim project alu.circ as structural Verilog: 1 circuit, main circuit alu
module alu (
  input  [31:0] A,
  input  [31:0] B,
  input  [3:0] ALUSel,
  output [31:0] Result
);

  wire less;
  wire [31:0] add, \and , div, mul, mulh, \or , rem, sll, slt, sra, srl, sub, \xor ;

  Shifter #(.width(32)) shifter_1 (.in(A), .\dist (B[4:0]), .out(sll));
  Shifter #(.width(32), .shift("lr")) shifter_2 (.in(A), .\dist (B[4:0]), .out(srl));
  Adder #(.width(32)) adder_1 (.a(A), .b(B), .out(add));  // open: cin, cout
  assign \and  = A & B;  // AND_Gate and_1, 32 bits wide
  assign \or  = A | B;  // OR_Gate or_1, 32 bits wide
  assign \xor  = A ^ B;  // XOR_Gate xor_1, 32 bits wide
  Comparator #(.width(32)) comparator_1 (.a(A), .b(B), .lt(less));  // open: gt, eq
  Multiplier #(.width(32)) multiplier_1 (.a(A), .b(B), .out(mul), .cout(mulh));  // open: cin
  Divider #(.width(32)) divider_1 (.a(A), .b(B), .out(div), .rem(rem));  // open: upper
  Shifter #(.width(32), .shift("ar")) shifter_3 (.in(A), .\dist (B[4:0]), .out(sra));
  Subtractor #(.width(32)) subtractor_1 (.a(A), .b(B), .out(sub));  // open: bin, bout
  Multiplexer #(.width(32), .enable("false")) multiplexer_1 (.in0({32{1'b0}}), .in1(32'h1), .out(slt), .sel(less));
  Multiplexer #(.select(4), .width(32), .enable("false")) multiplexer_2 (
    .in0(add), .in1(\and ), .in2(\or ), .in3(\xor ), .in4(srl), .in5(sra), .in6(sll), .in7(slt), .in8(div),
    .in9(rem), .in10(mul), .in11(mulh), .in12(sub), .in13(B), .out(Result), .sel(ALUSel));  // open: in14, in15

  // Notes on the sheet:
  //   INPUTS to your circuit
  //   DON'T CHANGE THE LOCATIONS OF THE INPUTS AND OUTPUTS!
  //   OUTPUT from your circuit
endmodule
