// Logisim project alu.circ as structural Verilog: 1 circuit, main circuit alu
module alu (
  input  [31:0] A,
  input  [31:0] B,
  input  [3:0] ALUSel,
  output [31:0] Result
);

  wire comparator_1_lt;
  wire [4:0] bit_extender_1_out, bit_extender_2_out, bit_extender_3_out;
  wire [31:0] add, and_ba9e6e9f, div_43d0fed6, mul_b0b3c26e, MULH, mulh_4ea149c4, mult1, mult2, mult3,
       multiplier_4_out, multiplier_5_out, negator_1_out, negator_2_out, or_443347e5, rem_870be134,
       sll_554dcb3c, slt_7af22b1d, sra_96dd6fa9, srl_ef4e7819, sub_86fcee41, xor_600234b1;

  Adder #(.width(32)) adder_1 (.a(A), .b(B), .out(add));  // open: cin, cout
  assign and_ba9e6e9f = A & B;  // AND_Gate and_1, 32 bits wide
  assign or_443347e5 = A | B;  // OR_Gate or_1, 32 bits wide
  assign xor_600234b1 = A ^ B;  // XOR_Gate xor_1, 32 bits wide
  Bit_Extender #(.in_width(32), .out_width(5)) bit_extender_1 (.in(B), .out(bit_extender_1_out));
  Bit_Extender #(.in_width(32), .out_width(5)) bit_extender_2 (.in(B), .out(bit_extender_2_out));
  Bit_Extender #(.in_width(32), .out_width(5)) bit_extender_3 (.in(B), .out(bit_extender_3_out));
  Comparator #(.width(32)) comparator_1 (.a(A), .b(B), .lt(comparator_1_lt));  // open: gt, eq
  Divider #(.width(32)) divider_1 (.a(A), .b(B), .out(div_43d0fed6));  // open: upper, rem
  Divider #(.width(32)) divider_2 (.a(A), .b(B), .rem(rem_870be134));  // open: out, upper
  Multiplier #(.width(32)) multiplier_1 (.a(A), .b(B), .out(mul_b0b3c26e));  // open: cin, cout
  Multiplier #(.width(32)) multiplier_2 (.a(A), .b(B), .cout(mulh_4ea149c4));  // open: out, cin
  Subtractor #(.width(32)) subtractor_1 (.a(A), .b(B), .out(sub_86fcee41));  // open: bin, bout
  Shifter #(.width(32), .shift("lr")) shifter_1 (.in(A), .\dist (bit_extender_1_out), .out(srl_ef4e7819));
  Shifter #(.width(32), .shift("ar")) shifter_2 (.in(A), .\dist (bit_extender_2_out), .out(sra_96dd6fa9));
  Shifter #(.width(32)) shifter_3 (.in(A), .\dist (bit_extender_3_out), .out(sll_554dcb3c));
  assign slt_7af22b1d = {{31{1'b0}}, comparator_1_lt};  // Bit_Extender bit_extender_4
  Negator #(.width(32)) negator_1 (.in(A), .out(negator_1_out));
  Negator #(.width(32)) negator_2 (.in(B), .out(negator_2_out));
  Multiplexer #(.select(4), .width(32), .enable("false")) multiplexer_1 (
    .in0(add), .in1(and_ba9e6e9f), .in2(or_443347e5), .in3(xor_600234b1), .in4(srl_ef4e7819),
    .in5(sra_96dd6fa9), .in6(sll_554dcb3c), .in7(slt_7af22b1d), .in8(div_43d0fed6), .in9(rem_870be134),
    .in10(mul_b0b3c26e), .in11(MULH), .in12(sub_86fcee41), .in13(B), .out(Result), .sel(ALUSel));  // open: in14, in15
  Multiplier #(.width(32)) multiplier_3 (.a(negator_1_out), .b(negator_2_out), .cout(mult3));  // open: out, cin
  Multiplier #(.width(32)) multiplier_4 (.a({32{1'b1}}), .b(B), .out(multiplier_4_out));  // open: cin, cout
  Multiplier #(.width(32)) multiplier_5 (.a({32{1'b1}}), .b(A), .out(multiplier_5_out));  // open: cin, cout
  Adder #(.width(32)) adder_2 (.a(mulh_4ea149c4), .b(multiplier_4_out), .out(mult1));  // open: cin, cout
  Adder #(.width(32)) adder_3 (.a(mulh_4ea149c4), .b(multiplier_5_out), .out(mult2));  // open: cin, cout
  Multiplexer #(.select(2), .width(32), .enable("false")) multiplexer_2 (
    .in0(mulh_4ea149c4), .in1(mult1), .in2(mult2), .in3(mult3), .out(MULH), .sel({B[31], A[31]}));

  // Other names for the same wires on the sheet: bsel[31:0] = B; A_31 = A[31]; SIGN[1:0] = {B[31], A[31]};
  //   B_31 = B[31]

  // Notes on the sheet:
  //   INPUTS to your circuit
  //   DON'T CHANGE THE LOCATIONS OF THE INPUTS AND OUTPUTS!
  //   OUTPUT from your circuit
endmodule
