// Logisim project mem.circ as structural Verilog: 1 circuit, main circuit main
module main (
  input  [31:0] Address,
  input  Write_En,
  input  clk,
  input  [31:0] Write_Data,
  output [31:0] Read_Data
);

  RAM #(.addrWidth(14), .dataWidth(32), .trigger("falling"), .databus("bibus")) ram_1 (
    .addr(Address[13:0]), .we(Write_En), .oe(1'b1), .clk(clk), .din(Write_Data), .dout(Read_Data));
endmodule
